# Fritzing sketch wiring (saved by Fritzing 0.9.6b)

parts:
  Part1 = Adafruit Metro with Headers [part_number="Adafruit #2488"]
  U1 = LCD-16X2 [package=lcd-16x2]
  LCM1602_IIC2 = LCM1602 IIC [part_number="LCM1602 IIC" chip_label="LCM1602 IIC" package="DIP (Dual Inline) [THT]"]

nets:
  N1: Part1.AD5/SCL, LCM1602_IIC2.SCL
  N2: Part1.AD4/SDA, LCM1602_IIC2.SDA
  +5V: Part1.+5V, LCM1602_IIC2.VCC
  GND: Part1.GND, LCM1602_IIC2.GND
  VSS: U1.VSS, LCM1602_IIC2.VSS
  VDD: U1.VDD, LCM1602_IIC2.VDD
  N3: U1.VO, LCM1602_IIC2.V0
  N4: U1.RS, LCM1602_IIC2.RS
  N5: U1.R_W, LCM1602_IIC2.RW
  N6: U1.E, LCM1602_IIC2.E
  N7: U1.DB0, LCM1602_IIC2.D0
  N8: U1.DB1, LCM1602_IIC2.D1
  N9: U1.DB2, LCM1602_IIC2.D2
  N10: U1.DB3, LCM1602_IIC2.D3
  N11: U1.DB4, LCM1602_IIC2.D4
  N12: U1.DB5, LCM1602_IIC2.D5
  N13: U1.DB6, LCM1602_IIC2.D6
  N14: U1.DB7, LCM1602_IIC2.D7
  N15: U1.A, LCM1602_IIC2.A
  N16: U1.K, LCM1602_IIC2.K

custom parts:
  Adafruit Metro with Headers: We sure love the ATmega328 here at Adafruit, and we use them a lot for our own projects. The processor has plenty of GPIO, Analog inputs, hardware UART SPI and I2C, timers and PWM galore - just enough for most simple projects. When we need to go small, we use a Pro Trinket 3V or 5V, but when size isn't as much of a concern, and an USB-serial converter is required, we reach for an Adafruit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
  LCM1602 IIC: I2C-Module to use a 1602 or 2004 LCD on with the wire.h libory Serial LCD Modul
