# Fritzing sketch wiring (saved by Fritzing 0.9.6b)

parts:
  J1 = Basic Servo
  Part1 = Adafruit Metro with Headers [part_number="Adafruit #2488"]

nets:
  GND: J1.gnd, Part1.GND
  VCC: J1.vcc, Part1.+5V
  N1: J1.pulse, Part1.IO5

custom parts:
  Adafruit Metro with Headers: We sure love the ATmega328 here at Adafruit, and we use them a lot for our own projects. The processor has plenty of GPIO, Analog inputs, hardware UART SPI and I2C, timers and PWM galore - just enough for most simple projects. When we need to go small, we use a Pro Trinket 3V or 5V, but when size isn't as much of a concern, and an USB-serial converter is required, we reach for an Adafruit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
